# Fritzing sketch fritzing_markoc (saved by Fritzing 0.9.3b)
breadboards: 1

parts:
  S2 = Pushbutton [package="[THT]"]
  S1 = Pushbutton [package="[THT]"]
  Part1 = Arduino Ethernet Shield (Rev3)
  Part2 = LCD1602-I2C

nets:
  N1: S2.Pin_1, S2.Pin_2, Part1.D8
  GND: S2.Pin_3, S2.Pin_4, S1.Pin_3, S1.Pin_4, Part1.GND, Part2.GND
  N2: S1.Pin_1, S1.Pin_2, Part1.PWM_D9
  N3: Part1.A4/SDA, Part2.SDA
  N4: Part1.A5/SCL, Part2.SCL
  3V3: Part1.3V3, Part2.VCC

custom parts:
  LCD1602-I2C: A standard character display, usually with 2x16 characters. Comes in many colors with LCM1602 IIC attached.

// code stored in the sketch: Untitled.ino
#include <Wire.h>
#include <LiquidCrystal_I2C.h>


LiquidCrystal_I2C lcd(0x27,16,2);


int BUT1=8;
int BUT2=9;


void setup(){
  lcd.init();
  lcd.backlight();
  pinMode(BUT1,INPUT_PULLUP);
  pinMode(BUT2,INPUT_PULLUP);
}


void loop(){
  if ((digitalRead(BUT1)==LOW) && (digitalRead(BUT2)==HIGH)){
    lcd.setCursor(0,1);
    lcd.clear();
    lcd.setCursor(0,0);
    lcd.print("Marko");
  }
  else if ((digitalRead(BUT1)==HIGH) && (digitalRead(BUT2)==LOW)){
    lcd.setCursor(0,0);
    lcd.clear();
    lcd.setCursor(0,1);
    lcd.print("Ciganovic");
  }
  else if ((digitalRead(BUT1)==LOW) && (digitalRead(BUT2)==LOW)){
    lcd.setCursor(0,0);
    lcd.clear();
    lcd.setCursor(0,0);
    lcd.print("Marko");
    lcd.setCursor(0,1);
    lcd.print("Ciganovic");
  }
}
